// Digital circuit alu.dig as structural Verilog
module alu (
  input  we,
  input  wclk,
  input  [7:0] a,
  input  [7:0] b,
  input  [2:0] opc3,
  output [7:0] res,
  output z,
  output n
);

  wire and_2_out, decoder_1_out_0, decoder_1_out_1, decoder_1_out_2, decoder_1_out_3, decoder_1_out_4,
       decoder_1_out_5, decoder_1_out_6, nor_1_out;
  wire [7:0] add_1_s, and_1_out, not_1_out, or_1_out, sub_1_s, xor_1_out;

  Add #(.Bits(8)) add_1 (.a(a), .b(b), .c_i(1'b0), .s(add_1_s));  // open: c_o
  Sub #(.Bits(8)) sub_1 (.a(a), .b(b), .c_i(1'b0), .s(sub_1_s));  // open: c_o
  assign and_1_out = a & b;  // And and_1, 8 bits wide
  assign or_1_out = a | b;  // Or or_1, 8 bits wide
  assign xor_1_out = a ^ b;  // XOr xor_1, 8 bits wide
  assign not_1_out = ~a;  // Not not_1, 8 bits wide
  assign res = decoder_1_out_1 ? add_1_s : 8'bz;  // Driver driver_1
  assign res = decoder_1_out_0 ? add_1_s : 8'bz;  // Driver driver_2
  assign res = decoder_1_out_2 ? sub_1_s : 8'bz;  // Driver driver_3
  assign res = decoder_1_out_3 ? and_1_out : 8'bz;  // Driver driver_4
  assign res = decoder_1_out_4 ? or_1_out : 8'bz;  // Driver driver_5
  assign res = decoder_1_out_5 ? xor_1_out : 8'bz;  // Driver driver_6
  assign res = decoder_1_out_6 ? not_1_out : 8'bz;  // Driver driver_7
  Decoder #(.Selector_Bits(3)) decoder_1 (
    .sel(opc3), .out_0(decoder_1_out_0), .out_1(decoder_1_out_1), .out_2(decoder_1_out_2),
    .out_3(decoder_1_out_3), .out_4(decoder_1_out_4), .out_5(decoder_1_out_5), .out_6(decoder_1_out_6));  // open: out_7
  and and_2 (and_2_out, wclk, we);
  nor nor_1 (nor_1_out, res[0], res[1], res[2], res[3], res[4], res[5], res[6], res[7]);
  D_FF u_Z (.D(nor_1_out), .C(and_2_out), .Q(z));  // open: nQ
  D_FF u_N (.D(res[7]), .C(and_2_out), .Q(n));  // open: nQ
endmodule
