// Digital circuit cwdecode.dig as structural Verilog
module cwdecode (
  input  [7:0] cw,
  output regs_we,
  output [1:0] regs_wd,
  output [1:0] alu_inb,
  output ram_str,
  output counter_jmp
);


  assign alu_inb = cw[4:3];
  assign counter_jmp = cw[1];
  assign ram_str = cw[2];
  assign regs_wd = cw[6:5];
  assign regs_we = cw[7];
endmodule
