// Digital circuit datasel.dig as structural Verilog
module datasel (
  input  [7:0] imm8,
  input  [7:0] alu_res,
  input  [7:0] regs_r2,
  input  [7:0] ram_d,
  input  [1:0] sel,
  output [7:0] dat
);

  wire decoder_1_out_0, decoder_1_out_1, decoder_1_out_2, decoder_1_out_3;

  assign dat = decoder_1_out_0 ? imm8 : 8'bz;  // Driver driver_1
  assign dat = decoder_1_out_1 ? alu_res : 8'bz;  // Driver driver_2
  assign dat = decoder_1_out_2 ? regs_r2 : 8'bz;  // Driver driver_3
  assign dat = decoder_1_out_3 ? ram_d : 8'bz;  // Driver driver_4
  Decoder #(.Selector_Bits(2)) decoder_1 (
    .sel(sel), .out_0(decoder_1_out_0), .out_1(decoder_1_out_1), .out_2(decoder_1_out_2),
    .out_3(decoder_1_out_3));
endmodule
