// Digital circuit decode.dig as structural Verilog
module decode (
  input  [15:0] inst,
  output [3:0] opc,
  output [2:0] reg1,
  output [2:0] reg2,
  output [5:0] imm6,
  output [7:0] imm8,
  output [2:0] opc3,
  output alu
);


  assign alu = inst[15];
  assign imm6 = inst[5:0];
  assign imm8 = inst[7:0];
  assign opc = inst[15:12];
  assign opc3 = inst[14:12];
  assign reg1 = inst[11:9];
  assign reg2 = inst[8:6];
endmodule
