// Digital circuit main.dig as structural Verilog
module main (
  input  clk,
  output wclk,
  output clk_2,
  output [15:0] out_4,
  output [7:0] R0,
  output [7:0] R1,
  output [7:0] A_ctrlrom
);

  wire and_2_out, cwdecode_1_counter_jmp, cwdecode_1_ram_str, cwdecode_1_regs_we, d_ff_1_q, decode_1_alu,
       not_1_out;
  wire [1:0] cwdecode_1_alu_inb, cwdecode_1_regs_wd;
  wire [2:0] decode_1_opc3, decode_1_reg1, decode_1_reg2;
  wire [7:0] counterpreset_1_out, ctrlrom_d, datasel_1_dat, datasel_2_dat, ds_1, ds_2, ds_3, ds_4, regs_1_r1,
       regs_1_r_ia;

  CounterPreset #(.Bits(8)) counterpreset_1 (
    .en(1'b1), .C(clk_2), .dir(1'b0), .in(regs_1_r_ia), .ld(cwdecode_1_counter_jmp), .clr(1'b0),
    .out(counterpreset_1_out));  // open: ovf
  EEPROM #(.AddrBits(8), .Bits(16)) instmem (.A(counterpreset_1_out), .CS(1'b1), .WE(1'b0), .OE(1'b1), .D(out_4));
  or or_1 (wclk, and_2_out, clk);
  decode decode_1 (
    .inst(out_4), .opc(A_ctrlrom[5:2]), .reg1(decode_1_reg1), .reg2(decode_1_reg2), .imm8(ds_1),
    .opc3(decode_1_opc3), .alu(decode_1_alu));  // open: imm6
  not not_1 (not_1_out, wclk);
  D_FF d_ff_1 (.D(wclk), .C(wclk), .Q(d_ff_1_q));  // open: nQ
  and and_1 (clk_2, not_1_out, d_ff_1_q);
  regs regs_1 (
    .wclk(wclk), .rs1(decode_1_reg1), .ws(decode_1_reg1), .we(cwdecode_1_regs_we), .wd(datasel_1_dat),
    .rs2(decode_1_reg2), .r1(regs_1_r1), .r2(ds_3), .r_IA(regs_1_r_ia), .TESTR0(R0), .TESTR1(R1));
  and and_2 (and_2_out, A_ctrlrom[2], A_ctrlrom[3], A_ctrlrom[4], A_ctrlrom[5]);
  RAMDualPort #(.AddrBits(8), .Bits(8)) ramdualport_1 (
    .A(regs_1_r_ia), .Din(regs_1_r1), .str(cwdecode_1_ram_str), .C(wclk), .ld(1'b1), .D(ds_4));
  alu alu_1 (
    .we(decode_1_alu), .wclk(wclk), .a(regs_1_r1), .b(datasel_2_dat), .opc3(decode_1_opc3), .res(ds_2),
    .z(A_ctrlrom[1]), .n(A_ctrlrom[0]));
  EEPROM #(.AddrBits(8), .Bits(8)) ctrlrom (
    .A({2'b00, A_ctrlrom[5:0]}), .CS(1'b1), .WE(1'b0), .OE(1'b1), .D(ctrlrom_d));
  cwdecode cwdecode_1 (
    .cw(ctrlrom_d), .regs_we(cwdecode_1_regs_we), .regs_wd(cwdecode_1_regs_wd), .alu_inb(cwdecode_1_alu_inb),
    .ram_str(cwdecode_1_ram_str), .counter_jmp(cwdecode_1_counter_jmp));
  datasel datasel_1 (
    .imm8(ds_1), .alu_res(ds_2), .regs_r2(ds_3), .ram_d(ds_4), .sel(cwdecode_1_regs_wd), .dat(datasel_1_dat));
  datasel datasel_2 (
    .imm8(ds_1), .alu_res(ds_2), .regs_r2(ds_3), .ram_d(ds_4), .sel(cwdecode_1_alu_inb), .dat(datasel_2_dat));

  assign A_ctrlrom[7:6] = 2'b00;

  // Other names for the same wires on the sheet: clk_t = clk_2

  // Notes on the sheet:
  //   clk: Hz: 10
  //   The P-8 Computer
  //   by Vardan Petrosyan
  //   December 2025
  //   contents of instmem (hex, n*v repeats v):
  //   2000,2201,2600,280a,1cc0,4000,2400,8400,8440,1040,1280,9601,1b00
  //   ,aac0,2c12,6000,2c04,5000,f000
  //   contents of ctrlrom (hex, n*v repeats v):
  //   4*0,4*c0,4*80,4*e0,4*4,4*2,0,0,2,2,0,2,0,2,4*b0,4*a0,20*b0
endmodule
