// Digital circuit mem.dig as structural Verilog
module mem (
  input  [7:0] A,
  input  [7:0] Din,
  input  str,
  input  C_write,
  output [7:0] D
);

  wire and_1_out, decoder_1_out_0, decoder_1_out_1;
  wire [7:0] ramasync_1_q;

  Decoder decoder_1 (.sel(A[7]), .out_0(decoder_1_out_0), .out_1(decoder_1_out_1));
  and and_1 (and_1_out, str, decoder_1_out_0, C_write);
  RAMAsync #(.AddrBits(8), .isProgramMemory("true"), .Bits(8)) ramasync_1 (
    .A(A), .D(Din), .we(and_1_out), .Q(ramasync_1_q));
  ROM #(.AddrBits(8), .isProgramMemory("true"), .Bits(8)) Program_ROM (
    .A({1'b0, A[6:0]}), .sel(decoder_1_out_1), .D(D));
  assign D = decoder_1_out_0 ? ramasync_1_q : 8'bz;  // Driver driver_1

  // Notes on the sheet:
  //   contents of Program_ROM (hex, n*v repeats v):
  //   1,2,3,4,5,6,7,8,9,a,9,8,7,6,5,4,3,2,1
endmodule
