// Digital circuit regs.dig as structural Verilog
module regs (
  input  wclk,
  input  [2:0] rs1,
  input  [2:0] ws,
  input  we,
  input  [7:0] wd,
  input  [2:0] rs2,
  output [7:0] r1,
  output [7:0] r2,
  output [7:0] r_IA,
  output [7:0] TESTR0,
  output [7:0] TESTR1
);

  wire and_2_out, and_3_out, and_4_out, and_5_out, and_6_out, and_7_out, and_8_out, and_9_out,
       decoder_1_out_0, decoder_1_out_1, decoder_1_out_2, decoder_1_out_3, decoder_1_out_4, decoder_1_out_5,
       decoder_1_out_6, decoder_1_out_7, decoder_2_out_0, decoder_2_out_1, decoder_2_out_2, decoder_2_out_3,
       decoder_2_out_4, decoder_2_out_5, decoder_2_out_6, decoder_2_out_7, decoder_3_out_0, decoder_3_out_1,
       decoder_3_out_2, decoder_3_out_3, decoder_3_out_4, decoder_3_out_5, decoder_3_out_6, decoder_3_out_7,
       w;
  wire [7:0] R2_q, R3_q, R4_q, R5_q, SP_q;

  Decoder #(.Selector_Bits(3)) decoder_1 (
    .sel(ws), .out_0(decoder_1_out_0), .out_1(decoder_1_out_1), .out_2(decoder_1_out_2),
    .out_3(decoder_1_out_3), .out_4(decoder_1_out_4), .out_5(decoder_1_out_5), .out_6(decoder_1_out_6),
    .out_7(decoder_1_out_7));
  and and_1 (w, we, wclk);
  and and_2 (and_2_out, w, decoder_1_out_0);
  and and_3 (and_3_out, w, decoder_1_out_1);
  and and_4 (and_4_out, w, decoder_1_out_2);
  and and_5 (and_5_out, w, decoder_1_out_3);
  and and_6 (and_6_out, w, decoder_1_out_4);
  and and_7 (and_7_out, w, decoder_1_out_5);
  and and_8 (and_8_out, w, decoder_1_out_6);
  and and_9 (and_9_out, w, decoder_1_out_7);
  D_FF #(.Bits(8)) R0 (.D(wd), .C(and_2_out), .Q(TESTR0));  // open: nQ
  D_FF #(.Bits(8)) u_R1 (.D(wd), .C(and_3_out), .Q(TESTR1));  // open: nQ
  D_FF #(.Bits(8)) u_R2 (.D(wd), .C(and_4_out), .Q(R2_q));  // open: nQ
  D_FF #(.Bits(8)) R3 (.D(wd), .C(and_5_out), .Q(R3_q));  // open: nQ
  D_FF #(.Bits(8)) R4 (.D(wd), .C(and_6_out), .Q(R4_q));  // open: nQ
  D_FF #(.Bits(8)) R5 (.D(wd), .C(and_7_out), .Q(R5_q));  // open: nQ
  D_FF #(.Bits(8)) IA (.D(wd), .C(and_8_out), .Q(r_IA));  // open: nQ
  D_FF #(.Bits(8)) SP (.D(wd), .C(and_9_out), .Q(SP_q));  // open: nQ
  assign r1 = decoder_2_out_0 ? TESTR0 : 8'bz;  // Driver driver_1
  assign r2 = decoder_3_out_0 ? TESTR0 : 8'bz;  // Driver driver_2
  assign r1 = decoder_2_out_1 ? TESTR1 : 8'bz;  // Driver driver_3
  assign r2 = decoder_3_out_1 ? TESTR1 : 8'bz;  // Driver driver_4
  assign r1 = decoder_2_out_2 ? R2_q : 8'bz;  // Driver driver_5
  assign r2 = decoder_3_out_2 ? R2_q : 8'bz;  // Driver driver_6
  assign r1 = decoder_2_out_3 ? R3_q : 8'bz;  // Driver driver_7
  assign r2 = decoder_3_out_3 ? R3_q : 8'bz;  // Driver driver_8
  assign r1 = decoder_2_out_4 ? R4_q : 8'bz;  // Driver driver_9
  assign r2 = decoder_3_out_4 ? R4_q : 8'bz;  // Driver driver_10
  assign r1 = decoder_2_out_5 ? R5_q : 8'bz;  // Driver driver_11
  assign r2 = decoder_3_out_5 ? R5_q : 8'bz;  // Driver driver_12
  assign r1 = decoder_2_out_6 ? r_IA : 8'bz;  // Driver driver_13
  assign r2 = decoder_3_out_6 ? r_IA : 8'bz;  // Driver driver_14
  assign r1 = decoder_2_out_7 ? SP_q : 8'bz;  // Driver driver_15
  assign r2 = decoder_3_out_7 ? SP_q : 8'bz;  // Driver driver_16
  Decoder #(.Selector_Bits(3)) decoder_2 (
    .sel(rs1), .out_0(decoder_2_out_0), .out_1(decoder_2_out_1), .out_2(decoder_2_out_2),
    .out_3(decoder_2_out_3), .out_4(decoder_2_out_4), .out_5(decoder_2_out_5), .out_6(decoder_2_out_6),
    .out_7(decoder_2_out_7));
  Decoder #(.Selector_Bits(3)) decoder_3 (
    .sel(rs2), .out_0(decoder_3_out_0), .out_1(decoder_3_out_1), .out_2(decoder_3_out_2),
    .out_3(decoder_3_out_3), .out_4(decoder_3_out_4), .out_5(decoder_3_out_5), .out_6(decoder_3_out_6),
    .out_7(decoder_3_out_7));

  // Notes on the sheet:
  //   we: default 1
  //   wd: default 7
endmodule
